# Fritzing sketch 4b3-LED+LED+Resistor_2.2KOhm+Resistor_47Ohm (saved by Fritzing 0.9.3b)
breadboards: 1

parts:
  Micro_bit1 = Microbit
  LED1 = LED - 5mm [color="Red (633nm)" package="5 mm [THT]"]
  R1 = Resistor [tolerance=±5% resistance=220 package=THT]
  LED2 = LED - 5mm [color="Red (633nm)" package="5 mm [THT]"]
  R2 = Resistor [tolerance=±5% resistance=220 package=THT]

nets:
  N1: Micro_bit1.GND, LED1.anode, LED2.anode
  N2: Micro_bit1.1, R1.Pin_0, R2.Pin_0
  N3: LED1.cathode, R1.Pin_1, LED2.cathode, R2.Pin_1

notes:
  Pin 1
  0v or GND Pin
  BBC micro:bit
  Breadboard
  LED
  2.2K Ohm
  +
  -
  47 Ohm

custom parts:
  Microbit: BBC Microbit Fritzing part
