# Fritzing sketch 4c2-NPN-BJT-Forward-Bias-Using-Pin2 (saved by Fritzing 0.9.3b)
breadboards: 1

parts:
  Micro_bit1 = Microbit
  LED1 = LED - 5mm [color="Red (633nm)" package="5 mm [THT]"]
  Q1 = NPN-Transistor [package="TO92 [THT]"]
  R2 = Resistor [tolerance=±5% resistance=220 package=THT]
  R1 = Resistor [tolerance=±5% resistance=220 package=THT]

nets:
  N1: Micro_bit1.GND, Q1.B
  N2: Micro_bit1.3V, R1.Pin_0
  N3: Micro_bit1.2, R2.Pin_0
  N4: LED1.cathode, R1.Pin_1
  N5: LED1.anode, Q1.E
  N6: Q1.C, R2.Pin_1

notes:
  Pin 2
  0v or GND Pin
  BBC micro:bit
  Breadboard
  LED
  2.2K Ohm
  +
  -
  47 Ohm
  C
  B
  E
  3V Pin

custom parts:
  Microbit: BBC Microbit Fritzing part
