# Fritzing sketch 4d2-Blinking_Multiple_LEDs (saved by Fritzing 0.9.3b)
breadboards: 1

parts:
  Micro_bit1 = Microbit
  LED1 = LED - 5mm [color="Red (633nm)" package="5 mm [THT]"]
  R1 = Resistor [tolerance=±5% resistance=220 package=THT]
  LED2 = LED - 5mm [color="Red (633nm)" package="5 mm [THT]"]
  R2 = Resistor [tolerance=±5% resistance=220 package=THT]

nets:
  N1: Micro_bit1.GND, LED1.anode, LED2.anode
  N2: Micro_bit1.1, R2.Pin_0
  N3: Micro_bit1.2, R1.Pin_0
  N4: LED1.cathode, R1.Pin_1
  N5: LED2.cathode, R2.Pin_1

notes:
  Pin 2
  0v or GND Pin
  BBC micro:bit
  Breadboard
  LED
  2.2K Ohm
  +
  -
  Pin 1

custom parts:
  Microbit: BBC Microbit Fritzing part
