# Fritzing sketch 4d3-Blinking_Multiple_LEDs_Additional_Resistors (saved by Fritzing 0.9.3b)
breadboards: 1

parts:
  Micro_bit1 = Microbit
  LED1 = LED - 5mm [color="Red (633nm)" package="5 mm [THT]"]
  R1 = Resistor [tolerance=±5% resistance=220 package=THT]
  LED2 = LED - 5mm [color="Red (633nm)" package="5 mm [THT]"]
  R2 = Resistor [tolerance=±5% resistance=220 package=THT]
  R3 = Resistor [tolerance=±5% resistance=220 package=THT]
  R4 = Resistor [tolerance=±5% resistance=220 package=THT]

nets:
  N1: Micro_bit1.GND, LED1.anode, LED2.anode
  N2: Micro_bit1.1, R2.Pin_0
  N3: Micro_bit1.2, R1.Pin_0
  N4: LED1.cathode, R4.Pin_1
  N5: R1.Pin_1, R4.Pin_0
  N6: LED2.cathode, R3.Pin_1
  N7: R2.Pin_1, R3.Pin_0

notes:
  Pin 2
  0v or GND Pin
  BBC micro:bit
  Breadboard
  LED
  2.2K Ohm
  +
  -
  Pin 1
  47 Ohm

custom parts:
  Microbit: BBC Microbit Fritzing part
