# Fritzing sketch 4d4-Blinking_Multiple_LEDs_Additional_Resistors_With_a_Transistor_and_Switch (saved by Fritzing 0.9.3b)
breadboards: 1

parts:
  Micro_bit1 = Microbit
  LED1 = LED - 5mm [color="Red (633nm)" package="5 mm [THT]"]
  R1 = Resistor [tolerance=±5% resistance=220 package=THT]
  LED2 = LED - 5mm [color="Red (633nm)" package="5 mm [THT]"]
  R2 = Resistor [tolerance=±5% resistance=220 package=THT]
  R3 = Resistor [tolerance=±5% resistance=220 package=THT]
  R4 = Resistor [tolerance=±5% resistance=220 package=THT]
  Q1 = NPN-Transistor [package="TO92 [THT]"]
  S1 = Pushbutton [package="[THT]"]

nets:
  N1: Micro_bit1.GND, LED1.anode, Q1.C
  N2: Micro_bit1.3V, R3.Pin_0
  N3: Micro_bit1.1, R2.Pin_0
  N4: Micro_bit1.2, R1.Pin_0
  N5: Micro_bit1.5, S1.Pin_3, S1.Pin_4
  N6: LED1.cathode, R4.Pin_1
  N7: R1.Pin_1, R4.Pin_0
  N8: LED2.cathode, R3.Pin_1
  N9: LED2.anode, Q1.E
  N10: R2.Pin_1, Q1.B

notes:
  Pin 2
  0v or GND Pin
  BBC micro:bit
  Breadboard
  LED
  2.2K Ohm
  +
  -
  Pin 1
  47 Ohm
  3V Pin
  C
  B
  E
  Pin 5
  Switch

custom parts:
  Microbit: BBC Microbit Fritzing part
