# Fritzing sketch 4e2-Control_RGB_LED_With_Potentiometer (saved by Fritzing 0.9.3b)
breadboards: 1

parts:
  Micro_bit1 = Microbit
  R1 = Resistor [tolerance=±5% resistance=220 package=THT]
  LED2 = RGB LED (com. cathode, rgb) [package="5 mm [THT]"]
  R3 = Resistor [tolerance=±5% resistance=220 package=THT]
  R2 = Resistor [tolerance=±5% resistance=220 package=THT]
  R4 = Rotary Potentiometer (Small) [maximum_resistance=100kΩ package=THT]

nets:
  N1: Micro_bit1.GND, LED2.common_cathode, R4.leg2
  N2: Micro_bit1.3V, R4.leg1
  N3: Micro_bit1.0, R1.Pin_0
  N4: Micro_bit1.1, R2.Pin_0
  N5: Micro_bit1.10, R4.wiper
  N6: Micro_bit1.2, R3.Pin_0
  N7: R1.Pin_1, LED2.red_anode
  N8: LED2.green_anode, R2.Pin_1
  N9: LED2.blue_anode, R3.Pin_1

notes:
  Pin 2
  0v Pin
  BBC micro:bit
  Breadboard
  +
  -
  R
  B
  G
  C
  Pin 1
  Pin 0
  2.2K Ohm
  3v Pin
  Pin 10

custom parts:
  Microbit: BBC Microbit Fritzing part
