# Fritzing sketch 4f1-Using _An_LDR_And_Measuring_Analog_Input (saved by Fritzing 0.9.3b)
breadboards: 1

parts:
  Micro_bit1 = Microbit
  R1 = Resistor [tolerance=±5% resistance=220 package=THT]
  R4 = Photocell (LDR) [package=THT]

nets:
  N1: Micro_bit1.GND, R1.Pin_1
  N2: Micro_bit1.3V, R4.pin_0
  N3: Micro_bit1.0, R1.Pin_0

notes:
  0v or GND Pin
  BBC micro:bit
  Breadboard
  +
  -
  R
  B
  G
  C
  Pin 0
  10K Ohm
  2.2K Ohm
  3v Pin

custom parts:
  Microbit: BBC Microbit Fritzing part
