# Fritzing sketch 4g1-Breadboard_Switches_In_Parallel_With_Main_Switch (saved by Fritzing 0.9.3b)
breadboards: 1

parts:
  Micro_bit1 = Microbit
  LED1 = LED - 5mm [color="Red (633nm)" package="5 mm [THT]"]
  R1 = Resistor [tolerance=±5% resistance=220 package=THT]

nets:
  N1: Micro_bit1.GND, LED1.anode
  N2: Micro_bit1.2, R1.Pin_0
  N3: LED1.cathode, R1.Pin_1

notes:
  Pin 2
  0v or GND Pin
  BBC micro:bit
  Breadboard
  LED
  2.2K Ohm
  +
  -

custom parts:
  Microbit: BBC Microbit Fritzing part
