# Fritzing sketch 4g2-Breadboard_Switches_In_Parallel_With_Main_Switch_and_LEDs (saved by Fritzing 0.9.3b)
breadboards: 1

parts:
  Micro_bit1 = Microbit
  S1 = Momentary Switch [package=ksa_sealed_tac_switch]
  S2 = Momentary Switch [package=ksa_sealed_tac_switch]
  LED1 = smd LED [color="Red (633nm)" package="0805 [SMD]"]
  LED2 = smd LED [color="Red (633nm)" package="0805 [SMD]"]
  R1 = Resistor [tolerance=±5% resistance=220 package=THT]
  R2 = Resistor [tolerance=±5% resistance=220 package=THT]
  LED4 = smd LED [color="Red (633nm)" package="0805 [SMD]"]

nets:
  N1: Micro_bit1.GND, S1.1, S2.1, LED1.anode, LED2.anode, LED4.anode
  N2: Micro_bit1.1, R1.Pin_0
  N3: Micro_bit1.2, R2.Pin_0
  N4: Micro_bit1.5, S1.3
  N5: Micro_bit1.11, S2.3
  N6: LED1.cathode, R1.Pin_1
  N7: LED2.cathode, R2.Pin_1, LED4.cathode

notes:
  Pin 5
  0v or GND Pin
  BBC micro:bit
  Breadboard
  +
  -
  Pin 11
  Switch 1
  Switch 2
  Pin 1
  Pin 2
  LED
  2.2K Ohm

custom parts:
  Microbit: BBC Microbit Fritzing part
