# Fritzing sketch 4h1-Dimming_An_LED_Using_A_Potentiometer (saved by Fritzing 0.9.3b)
breadboards: 1

parts:
  Micro_bit1 = Microbit
  LED1 = LED - 5mm [color="Red (633nm)" package="5 mm [THT]"]
  R1 = Resistor [tolerance=±5% resistance=220 package=THT]
  R2 = Rotary Potentiometer (Small) [maximum_resistance=100kΩ package=THT]
  S1 = Pushbutton [package="[SMD]"]

nets:
  N1: Micro_bit1.GND, LED1.anode, R2.leg1, S1.Pin_1, S1.Pin_2
  N2: Micro_bit1.3V, R2.leg2
  N3: Micro_bit1.0, S1.Pin_3, S1.Pin_4
  N4: Micro_bit1.1, R2.wiper
  N5: Micro_bit1.2, R1.Pin_0
  N6: LED1.cathode, R1.Pin_1

notes:
  Pin 0
  0v or GND Pin
  BBC micro:bit
  Breadboard
  LED
  2.2K Ohm
  +
  -
  Pin 1
  Pin 2
  3v Pin
  Switch

custom parts:
  Microbit: BBC Microbit Fritzing part
