# Fritzing sketch 4i1-Using_A_Transistor_To_Drive_A_Motor (saved by Fritzing 0.9.3b)
breadboards: 1

parts:
  Micro_bit1 = Microbit
  R1 = Resistor [tolerance=±5% resistance=220 package=THT]
  Q1 = NPN-Transistor [package="TO92 [THT]"]
  M1 = DC Motor

nets:
  N1: Micro_bit1.GND, Q1.E
  N2: Micro_bit1.3V, R1.Pin_0, M1.pin_2
  N3: R1.Pin_1, Q1.B
  N4: Q1.C, M1.pin_1

notes:
  Pin 3v
  0v or GND Pin
  BBC micro:bit
  Breadboard
  2.2K Ohm
  +
  -
  E
  B
  C
  NPN Transistor
  Motor

custom parts:
  Microbit: BBC Microbit Fritzing part
